# Fritzing sketch ac-infinity-esphome (saved by Fritzing 1.0.4)
circuit board: 6.9803cm x 5.70088cm
breadboards: 1

parts:
  U1 = ESP32-38PinWide [part_number=ESP32-38PinWide]
  C1 = Tantalum Capacitor [capacitance=0.1µF voltage=35V package="100 mil [THT, tantalum]"]
  Q1 = NPN-Transistor [package="TO92 [THT]"]
  JP2 = Header 4 [package=screwterminal-3.5mm-4_lock]
  C2 = Tantalum Capacitor [capacitance=0.1µF voltage=35V package="100 mil [THT, tantalum]"]
  Q2 = NPN-Transistor [package="TO92 [THT]"]
  R1 = Resistor [tolerance=±5% resistance=100k power=0.25W package=THT]
  R2 = Resistor [tolerance=±5% resistance=10k power=0.25W package=THT]
  R7 = Resistor [tolerance=±5% resistance=1k power=0.25W package=THT]
  R4 = Resistor [tolerance=±5% resistance=10k power=0.25W package=THT]
  R6 = Resistor [tolerance=±5% resistance=100k power=0.25W package=THT]
  R3 = Resistor [tolerance=±5% resistance=4.7k power=0.25W package=THT]
  JP1 = Header 4 [package=screwterminal-3.5mm-4_lock]
  Relay = DPDT Relay [chip_label=Relay package="DIP (Dual Inline) [THT]"]
  D1 = Diode [package=diode-1n4148]
  Q3 = NPN-Transistor [package="TO92 [THT]"]
  R8 = Resistor [tolerance=±5% resistance=1k power=0.25W package=THT]
  U2 = Voltage Regulator - 5V [package="TO220 [THT]"]
  C3 = Tantalum Capacitor [capacitance=0.47µF voltage=35V package="200 mil [THT, tantalum]"]
  Q4 = NPN-Transistor [package="TO92 [THT]"]
  R9 = Resistor [tolerance=±5% resistance=1k power=0.25W package=THT]
  R10 = Resistor [tolerance=±5% resistance=1k power=0.25W package=THT]

nets:
  N1: U1.3.3, R1.Pin_1, R4.Pin_1, R6.Pin_1
  N2: U1.GPIO34, R4.Pin_0, R3.Pin_0, C3.+
  N3: U1.GPIO33, Q1.C, R6.Pin_0
  N4: U1.GPIO25, Q2.C, R1.Pin_0, R3.Pin_1
  N5: U1.GPIO26, R9.Pin_1
  N6: U1.GPIO27, R8.Pin_0
  GND: U1.GND, C1.-, Q1.E, JP2.4, C2.-, Q2.E, JP1.4, Q3.E, U2.GND, C3.-, Q4.E
  N7: U1.VIN, C1.+, Relay.pin8, D1.C, U2.output_voltage
  N8: Q1.B, R7.Pin_1
  N9: JP2.1, C2.+, JP1.1, U2.input_voltage, R10.Pin_1
  N10: JP2.2, R7.Pin_0, JP1.2
  N11: JP2.3, Relay.pin2
  N12: Q2.B, R2.Pin_0
  N13: R2.Pin_1, JP1.3, Relay.pin3
  N14: Relay.pin1, D1.A, Q3.C
  N15: Relay.pin4, Q4.C, R10.Pin_0
  N16: Q3.B, R8.Pin_1
  N17: Q4.B, R9.Pin_0

notes:
  HA-AC-Infinity Rev.3.1
  R
  Y
  W
  B

custom parts:
  ESP32-38PinWide: Generic 38-Pin ESP32 with wide format (only access to one side of pins on a breadboard) based on Stephen Lilley's HiLetgo ESP-WROOM-32 ESP32 ESP-32S Development Board.
  DPDT Relay: DIP DPDT Relay (Double Pole Double Throw)
